// Logisim project Regfile.circ as structural Verilog: 2 circuits, main circuit main
module main (
  input  [1:0] Read_register_1,
  input  [1:0] Read_register_2,
  input  [1:0] write_register,
  input  [15:0] write_data,
  input  RegWrite,
  input  clock,
  output [15:0] Reg_0_Value,
  output [15:0] Reg_1_Value,
  output [15:0] Reg_2_Value,
  output [15:0] Reg_3_Value,
  output [15:0] Read_Data_1,
  output [15:0] Read_Data_2
);

  wire _0, _1, _2, _3;
  wire [15:0] multiplexer_1_out, multiplexer_2_out, multiplexer_3_out, multiplexer_4_out, r0_in, r1_in,
       r2_in, r3_in;

  Demultiplexer #(.select(2), .width(16), .enable("false")) demultiplexer_1 (
    .out0(r0_in), .out1(r1_in), .out2(r2_in), .out3(r3_in), .in(write_data), .sel(write_register));
  register_selector register_selector_1 (
    .regWrite(RegWrite), .write_reg(write_register), ._0(_0), ._1(_1), ._2(_2), ._3(_3));
  Multiplexer #(.width(16), .enable("false")) multiplexer_1 (
    .in0(Reg_0_Value), .in1(r0_in), .out(multiplexer_1_out), .sel(_0));
  Multiplexer #(.width(16), .enable("false")) multiplexer_2 (
    .in0(Reg_1_Value), .in1(r1_in), .out(multiplexer_2_out), .sel(_1));
  Multiplexer #(.width(16), .enable("false")) multiplexer_3 (
    .in0(Reg_2_Value), .in1(r2_in), .out(multiplexer_3_out), .sel(_2));
  Multiplexer #(.width(16), .enable("false")) multiplexer_4 (
    .in0(Reg_3_Value), .in1(r3_in), .out(multiplexer_4_out), .sel(_3));
  Register #(.width(16)) r0 (.D(multiplexer_1_out), .Q(Reg_0_Value), .clk(clock));  // open: en, clr
  Register #(.width(16)) r1 (.D(multiplexer_2_out), .Q(Reg_1_Value), .clk(clock));  // open: en, clr
  Register #(.width(16)) r2 (.D(multiplexer_3_out), .Q(Reg_2_Value), .clk(clock));  // open: en, clr
  Register #(.width(16)) r3 (.D(multiplexer_4_out), .Q(Reg_3_Value), .clk(clock));  // open: en, clr
  Multiplexer #(.select(2), .width(16), .enable("false")) multiplexer_5 (
    .in0(Reg_0_Value), .in1(Reg_1_Value), .in2(Reg_2_Value), .in3(Reg_3_Value), .out(Read_Data_1),
    .sel(Read_register_1));
  Multiplexer #(.select(2), .width(16), .enable("false")) multiplexer_6 (
    .in0(Reg_0_Value), .in1(Reg_1_Value), .in2(Reg_2_Value), .in3(Reg_3_Value), .out(Read_Data_2),
    .sel(Read_register_2));

  // Other names for the same wires on the sheet: r0_out[15:0] = Reg_0_Value; r1_out[15:0] = Reg_1_Value;
  //   r2_out[15:0] = Reg_2_Value; r3_out[15:0] = Reg_3_Value; read_reg1[1:0] = Read_register_1;
  //   read_reg2[1:0] = Read_register_2; write_reg[1:0] = write_register

  // Notes on the sheet:
  //   These are INPUTS to the circuit
  //   data selector
  //   These are INPUTS to the circuit
  //   DO NOT CHANGE THE LOCATIONS OF THE INPUTS/OUTPUTS! IF YOU DO SO, YOU NEED TO MAKE SURE THE PINS ARE AT THE RIGHT PLACE!
  //   register selector
  //   These are OUTPUTS to the circuit
  //   Yet again, the clock is not an actual clock, but an input, one that will be driven from a higher circuit
  //   These are OUTPUTS to the circuit
endmodule

module register_selector (
  input  regWrite,
  input  [1:0] write_reg,
  output _0,
  output _1,
  output _2,
  output _3
);

  wire _0_t, _1_t, _2_t, _3_t;

  Demultiplexer #(.select(2), .enable("false")) demultiplexer_1 (
    .out0(_0_t), .out1(_1_t), .out2(_2_t), .out3(_3_t), .in(1'b1), .sel(write_reg));
  and and_1 (_0, regWrite, _0_t);
  and and_2 (_1, regWrite, _1_t);
  and and_3 (_2, regWrite, _2_t);
  and and_4 (_3, regWrite, _3_t);
endmodule
