// Logisim project alu.circ as structural Verilog: 3 circuits, main circuit main
module main (
  input  [15:0] X,
  input  [15:0] Y,
  input  [3:0] Switch__S,
  output Signed_Overflow,
  output [15:0] RESULT,
  output Equal
);

  wire aof, aof_high, aof_low, ap8_of, slt, sof, sof_high, sof_low, sp8_of;
  wire [7:0] high_diff, low_diff;
  wire [15:0] add_out, addp8_out, and_out, or_out, sllv_out, srav_out, srlv_out, sub_out;

  Adder #(.width(16)) adder_1 (.a(X), .b(Y), .out(add_out));  // open: cin, cout
  Subtractor #(.width(16)) subtractor_1 (.a(X), .b(Y), .out(sub_out));  // open: bin, bout
  Shifter #(.width(16)) shifter_1 (.in(X), .\dist (Y[3:0]), .out(sllv_out));
  Shifter #(.width(16), .shift("lr")) shifter_2 (.in(X), .\dist (Y[3:0]), .out(srlv_out));
  overflow_check overflow_check_1 (.x(X), .y(Y), ._16bit_sum(add_out), ._16bit_diff(sub_out), .add(aof), .sub(sof));
  Shifter #(.width(16), .shift("ar")) shifter_3 (.in(X), .\dist (Y[3:0]), .out(srav_out));
  Comparator #(.width(16)) comparator_1 (.a(X), .b(Y), .lt(slt));  // open: gt, eq
  assign or_out = X | Y;  // OR_Gate or_1, 16 bits wide
  assign and_out = X & Y;  // AND_Gate and_1, 16 bits wide
  or or_2 (ap8_of, aof_low, aof_high);
  _8bit_check u_8bit_check_1 (
    .x(X[7:0]), .y(Y[7:0]), ._8bit_sum(addp8_out[7:0]), ._8bit_diff(low_diff), .add(aof_low), .sub(sof_low));
  Adder adder_2 (.a(X[7:0]), .b(Y[7:0]), .out(addp8_out[7:0]));  // open: cin, cout
  Adder adder_3 (.a(X[15:8]), .b(Y[15:8]), .out(addp8_out[15:8]));  // open: cin, cout
  Subtractor subtractor_2 (.a(X[7:0]), .b(Y[7:0]), .out(low_diff));  // open: bin, bout
  Subtractor subtractor_3 (.a(X[15:8]), .b(Y[15:8]), .out(high_diff));  // open: bin, bout
  or or_3 (sp8_of, sof_low, sof_high);
  _8bit_check u_8bit_check_2 (
    .x(X[15:8]), .y(Y[15:8]), ._8bit_sum(addp8_out[15:8]), ._8bit_diff(high_diff), .add(aof_high),
    .sub(sof_high));
  Multiplexer #(.select(4), .enable("false")) multiplexer_1 (
    .in0(aof), .in1(sof), .in8(ap8_of), .in9(sp8_of), .out(Signed_Overflow), .sel(Switch__S));  // open: in2, in3, in4, in5, in6, in7, in10, in11, in12, in13, in14, in15
  Multiplexer #(.select(4), .width(16), .enable("false")) multiplexer_2 (
    .in0(add_out), .in1(sub_out), .in2(sllv_out), .in3(srlv_out), .in4(srav_out), .in5({{15{1'b0}}, slt}),
    .in6(or_out), .in7(and_out), .in8(addp8_out), .in9({high_diff, low_diff}), .out(RESULT), .sel(Switch__S));  // open: in10, in11, in12, in13, in14, in15
  Comparator #(.width(16)) comparator_2 (.a(X), .b(Y), .eq(Equal));  // open: gt, lt

  // Other names for the same wires on the sheet: low_sum[7:0] = addp8_out[7:0]; high_sum[7:0] = addp8_out[15:8];
  //   slt_out[0] = slt; subp8_out[15:0] = {high_diff, low_diff}; switch[3:0] = Switch__S; x_low[7:0] = X[7:0];
  //   x_high[7:0] = X[15:8]; y_4bits[3:0] = Y[3:0]; y_low[7:0] = Y[7:0]; y_high[7:0] = Y[15:8]

  // Notes on the sheet:
  //   INPUTS to your circuit
  //   INPUT to your circuit
  //   check 16bit signed overflow
  //   add
  //   sub
  //   sllv
  //   srlv
  //   extend slt
  //   DON'T CHANGE THE INPUTS AND OUTPUTS! IF YOU DO SO, YOU NEED TO MAKE SURE THE PINS ARE IN THE RIGHT PLACES!
  //   srav
  //   slt
  //   or
  //   and
  //   check for addp8 overflow
  //   check 8bit low overflow
  //   addp8
  //   subp8
  //   check for subp8 overflow
  //   check 8bit high overflow
  //   OUTPUTS of your circuit
endmodule

module overflow_check (
  input  [15:0] x,
  input  [15:0] y,
  input  [15:0] _16bit_sum,
  input  [15:0] _16bit_diff,
  output add,
  output sub
);

  wire and_5_out, and_6_out, and_7_out, and_8_out, diff_negative, diff_positive, negative_inputs, not_1_out,
       not_2_out, not_3_out, not_4_out, not_5_out, positive_inputs, sum_negative, sum_positive, tunnel,
       tunnel_t;

  Comparator #(.width(16)) comparator_1 (
    .a(_16bit_sum), .b({16{1'b0}}), .gt(sum_positive), .lt(sum_negative));  // open: eq
  Comparator #(.width(16)) comparator_2 (
    .a(_16bit_diff), .b({16{1'b0}}), .gt(diff_positive), .lt(diff_negative));  // open: eq
  not not_1 (not_1_out, x[15]);
  not not_2 (not_2_out, y[15]);
  not not_3 (not_3_out, y[15]);
  not not_4 (not_4_out, x[15]);
  and and_1 (negative_inputs, x[15], y[15]);
  and and_2 (positive_inputs, not_1_out, not_2_out);
  and and_3 (tunnel_t, x[15], not_3_out);
  and and_4 (tunnel, not_4_out, y[15]);
  not not_5 (not_5_out, sum_negative);
  and and_5 (and_5_out, positive_inputs, sum_negative);
  and and_6 (and_6_out, negative_inputs, not_5_out);
  and and_7 (and_7_out, tunnel_t, diff_positive);
  and and_8 (and_8_out, tunnel, diff_negative);
  or or_1 (add, and_5_out, and_6_out);
  or or_2 (sub, and_7_out, and_8_out);

  // Other names for the same wires on the sheet: x_sign = x[15]; y_sign = y[15]
endmodule

module _8bit_check (
  input  [7:0] x,
  input  [7:0] y,
  input  [7:0] _8bit_sum,
  input  [7:0] _8bit_diff,
  output add,
  output sub
);

  wire and_5_out, and_6_out, and_7_out, and_8_out, diff_negative, diff_positive, negative_inputs, not_1_out,
       not_2_out, not_3_out, not_4_out, not_5_out, positive_inputs, sum_negative, sum_positive, tunnel,
       tunnel_t;

  Comparator comparator_1 (.a(_8bit_sum), .b({8{1'b0}}), .gt(sum_positive), .lt(sum_negative));  // open: eq
  Comparator comparator_2 (.a(_8bit_diff), .b({8{1'b0}}), .gt(diff_positive), .lt(diff_negative));  // open: eq
  not not_1 (not_1_out, x[7]);
  not not_2 (not_2_out, y[7]);
  not not_3 (not_3_out, y[7]);
  not not_4 (not_4_out, x[7]);
  and and_1 (negative_inputs, x[7], y[7]);
  and and_2 (positive_inputs, not_1_out, not_2_out);
  and and_3 (tunnel_t, x[7], not_3_out);
  and and_4 (tunnel, not_4_out, y[7]);
  not not_5 (not_5_out, sum_negative);
  and and_5 (and_5_out, positive_inputs, sum_negative);
  and and_6 (and_6_out, negative_inputs, not_5_out);
  and and_7 (and_7_out, tunnel_t, diff_positive);
  and and_8 (and_8_out, tunnel, diff_negative);
  or or_1 (add, and_5_out, and_6_out);
  or or_2 (sub, and_7_out, and_8_out);

  // Other names for the same wires on the sheet: x_sign = x[7]; y_sign = y[7]
endmodule
