// Logisim project cpu.circ as structural Verilog: 12 circuits, main circuit main
// nop
module main (
  input  [15:0] From_Instr_Mem,
  input  clk,
  output [15:0] r0,
  output [15:0] r1,
  output [15:0] r2,
  output [15:0] r3,
  output [15:0] Display_0,
  output [15:0] Display_1,
  output [15:0] To_Instr_Mem,
  output [15:0] Data_Mem_Data,
  output [15:0] Data_Mem_Addr,
  output Data_Mem_Write
);

  wire addi, andi, b_j, beq, bne, branch, disp, disp0, disp1, Equal, j, jal, jr, jump, lui, lw, ori,
       overflow, R_type, RegWrite;
  wire [1:0] rs, rt, writeReg;
  wire [3:0] opcode, switch;
  wire [5:0] funct;
  wire [7:6] imm;
  wire [15:0] alu_out, branchPC, currPC, data_mem_out, jumpPC, multiplexer_1_out, reg1_data, regWriteData, x,
       y;

  new_PC new_pc_1 (
    .nextPC(To_Instr_Mem), .branchPC(branchPC), .branch(branch), .jump(jump), .jumpPC(jumpPC), .clk(clk),
    .newPC(To_Instr_Mem));
  Demultiplexer #(.select(4), .enable("false")) demultiplexer_1 (
    .out0(R_type), .out1(jal), .out2(j), .out3(jr), .out4(beq), .out5(addi), .out6(andi), .out7(ori),
    .out8(bne), .out9(Data_Mem_Write), .out10(lui), .out11(lw), .out12(disp), .in(1'b1), .sel(opcode));  // open: out13, out14, out15
  // Probe on To_Instr_Mem
  Multiplexer #(.width(16), .enable("false")) multiplexer_1 (
    .in0(From_Instr_Mem), .in1(16'h6), .out(multiplexer_1_out), .sel(b_j));
  // Probe on currPC
  Register #(.width(16)) register_1 (.D(To_Instr_Mem), .Q(currPC), .clk(clk));  // open: en, clr
  Register #(.width(16)) register_2 (
    .D(multiplexer_1_out), .Q({opcode, rs, rt, imm, funct}), .clk(clk));  // open: en, clr
  Mem_Address mem_address_1 (.rs(reg1_data), .imm({imm, funct}), .mem_addr(Data_Mem_Addr));
  Regfile_main main_1 (
    .Read_register_1(rs), .Read_register_2(rt), .write_register(writeReg), .write_data(regWriteData),
    .Reg_0_Value(r0), .Reg_1_Value(r1), .Reg_2_Value(r2), .Reg_3_Value(r3), .RegWrite(RegWrite), .clock(clk),
    .Read_Data_1(reg1_data), .Read_Data_2(Data_Mem_Data));
  display_selector display_selector_1 (.disp(disp), .immediate({imm, funct}), .disp0(disp0), .disp1(disp1));
  Branch_Calc branch_calc_1 (
    .imm({imm, funct}), .currPC(currPC), .beq(beq), .bne(bne), .equal(Equal), .branchPC(branchPC),
    .branch(branch));
  alu_main ALU (.Switch__S(switch), .X(x), .Equal(Equal), .RESULT(alu_out), .Signed_Overflow(overflow), .Y(y));
  RegWrite regwrite_1 (.opcode(opcode), .RegWrite(RegWrite));
  input_selector input_selector_1 (
    .rs(reg1_data), .rt(Data_Mem_Data), .imm({imm, funct}), .opcode(opcode), .x(x), .y(y));
  jumps jumps_1 (
    .target_addr({rs, rt, imm, funct}), .currPC(currPC), .rs(reg1_data), .jal(jal), .j(j), .jr(jr),
    .jump(jump), .jumpPC(jumpPC));
  switcher switcher_1 (.funct(funct), .opcode(opcode), .switch(switch));
  Write_Selector write_selector_1 (
    .ALU_out(alu_out), .mem(data_mem_out), .op(opcode), .currPC(currPC), .rt(rt), .rd(imm), .write(writeReg),
    .writeData(regWriteData));
  or or_1 (b_j, branch, jump);
  Data_Memory Data_Memory (
    .Data_In(Data_Mem_Data), .Address(Data_Mem_Addr), .MemWrite(Data_Mem_Write), .clk(clk), .Reset(1'b0),
    .Data_Out(data_mem_out));
  Hex_Digit_Display hex_digit_display_1 (.value(Display_0[15:12]));  // open: dp
  Hex_Digit_Display hex_digit_display_2 (.value(Display_1[15:12]));  // open: dp
  Hex_Digit_Display hex_digit_display_3 (.value(Display_0[7:4]));  // open: dp
  Hex_Digit_Display hex_digit_display_4 (.value(Display_0[11:8]));  // open: dp
  Register #(.width(16)) register_3 (.D(reg1_data), .en(disp0), .Q(Display_0), .clk(clk));  // open: clr
  Hex_Digit_Display hex_digit_display_5 (.value(Display_1[7:4]));  // open: dp
  Hex_Digit_Display hex_digit_display_6 (.value(Display_1[11:8]));  // open: dp
  Register #(.width(16)) register_4 (.D(reg1_data), .en(disp1), .Q(Display_1), .clk(clk));  // open: clr
  LED led_1 (.in(overflow));
  Hex_Digit_Display hex_digit_display_7 (.value(Display_0[3:0]));  // open: dp
  Hex_Digit_Display hex_digit_display_8 (.value(Display_1[3:0]));  // open: dp

  // Other names for the same wires on the sheet: clock = clk; d0[15:0] = Display_0; d0_0[3:0] = Display_0[3:0];
  //   d0_1[3:0] = Display_0[7:4]; d0_2[3:0] = Display_0[11:8]; d0_3[3:0] = Display_0[15:12]; d1[15:0] = Display_1;
  //   d1_0[3:0] = Display_1[3:0]; d1_1[3:0] = Display_1[7:4]; d1_2[3:0] = Display_1[11:8];
  //   d1_3[3:0] = Display_1[15:12]; imm[5:0] = funct; target_addr[11:0] = {rs, rt, imm, funct}; rd[1:0] = imm;
  //   nextPC[15:0] = To_Instr_Mem; reg2_data[15:0] = Data_Mem_Data; sw = Data_Mem_Write

  // Notes on the sheet:
  //   instruction decoding
  //   This is the current PC that you need to send as OUTPUT
  //   This is the instruction that you would receive as INPUT
  //   PIPELINE
  //   This is a CLK that is an INPUT driven from the harness ->
  //   kill
  //   DO NOT CHANGE THE LOCATIONS OF THE INPUTS OR OUTPUTS! IF YOU DO SO, YOU NEED TO MAKE SURE THE PINS ARE IN THE RIGHT PLACES!
  //   construct immediate
  //   construct target address
  //   These are OUTPUTS of the circuit
  //   display selector
  //   calc data mem addr
  //   register
  //   MAIN CONTROL
  //   branching
  //   RegWrite Mux
  //   DATA PATH (Registers, ALU, Data Mem)
  //   alu input selector
  //   BRANCHING AND JUMPING CONTROL
  //   jumping
  //   switcher
  //   Write selector
  //   branch/jump
  //   reset
  //   DISPLAY 0
  //   DISPLAY 1
  //   OUTPUT DEVICES
  //   These are OUTPUTS of the circuit
  //   overflow
  //   indicator
endmodule

module Data_Memory (
  input  [15:0] Data_In,
  input  [15:0] Address,
  input  clk,
  input  Reset,
  input  MemWrite,
  output [15:0] Data_Out
);

  wire not_1_out;

  not not_1 (not_1_out, MemWrite);
  assign Data_Out = MemWrite ? Data_In : 16'bz;  // Controlled_Buffer controlled_buffer_1
  RAM #(.addrWidth(16), .dataWidth(16)) ram_1 (
    .addr(Address), .data(Data_Out), .sel(1'b1), .clk(clk), .ld(not_1_out), .clr(Reset));
endmodule

module display_selector (
  input  disp,
  input  [7:0] immediate,
  output disp0,
  output disp1
);

  wire comparator_1_eq, comparator_2_eq;

  Comparator #(.mode("unsigned")) comparator_1 (.a(immediate), .b({8{1'b0}}), .eq(comparator_1_eq));  // open: gt, lt
  Comparator #(.mode("unsigned")) comparator_2 (.a(immediate), .b(8'h1), .eq(comparator_2_eq));  // open: gt, lt
  and and_1 (disp0, disp, comparator_1_eq);
  and and_2 (disp1, disp, comparator_2_eq);

  // Other names for the same wires on the sheet: imm[7:0] = immediate
endmodule

module imm_extension (
  input  [7:0] imm,
  output [15:0] \unsigned ,
  output [15:0] \signed 
);

  wire and_1_out;

  and and_1 (and_1_out, imm[7], 1'b1);
  Multiplexer #(.width(16), .enable("false")) multiplexer_1 (
    .in0({{8{1'b0}}, imm}), .in1({{8{1'b1}}, imm}), .out(\signed ), .sel(and_1_out));

  assign \unsigned  = {{8{1'b0}}, imm};

  // Notes on the sheet:
  //   if imm is negative, extend by 1's, else extend by zeros
endmodule

module switcher (
  input  [5:0] funct,
  input  [3:0] opcode,
  output [3:0] switch
);

  Multiplexer #(.select(4), .width(4), .enable("false")) multiplexer_1 (
    .in0(funct[3:0]), .in5(4'b0000), .in6(4'b0111), .in7(4'b0110), .in10(4'b0010), .out(switch), .sel(opcode));  // open: in1, in2, in3, in4, in8, in9, in11, in12, in13, in14, in15

  // Notes on the sheet:
  //   addi
  //   andi
  //   ori
  //   lui
endmodule

module input_selector (
  input  [15:0] rs,
  input  [15:0] rt,
  input  [7:0] imm,
  input  [3:0] opcode,
  output [15:0] x,
  output [15:0] y
);

  wire [15:0] \signed , \unsigned ;

  imm_extension imm_extension_1 (.imm(imm), .\unsigned (\unsigned ), .\signed (\signed ));
  Multiplexer #(.select(4), .width(16), .enable("false")) multiplexer_1 (
    .in0(rs), .in4(rs), .in5(rs), .in6(rs), .in7(rs), .in8(rs), .in10(\unsigned ), .out(x), .sel(opcode));  // open: in1, in2, in3, in9, in11, in12, in13, in14, in15
  Multiplexer #(.select(4), .width(16), .enable("false")) multiplexer_2 (
    .in0(rt), .in4(rt), .in5(\signed ), .in6(\unsigned ), .in7(\unsigned ), .in8(rt), .in10(16'h8), .out(y),
    .sel(opcode));  // open: in1, in2, in3, in9, in11, in12, in13, in14, in15

  // Other names for the same wires on the sheet: op[3:0] = opcode

  // Notes on the sheet:
  //   bne
  //   andi
  //   ori
  //   bne
  //   beq
  //   addi
  //   addi
  //   andi
  //   ori
  //   lui
  //   lui
endmodule

module Write_Selector (
  input  [1:0] rt,
  input  [1:0] rd,
  input  [15:0] ALU_out,
  input  [15:0] mem,
  input  [3:0] op,
  input  [15:0] currPC,
  output [1:0] write,
  output [15:0] writeData
);

  wire [15:0] store;

  Adder #(.width(16)) adder_1 (.a(currPC), .b(16'h1), .out(store));  // open: cin, cout
  Multiplexer #(.select(4), .width(2), .enable("false")) multiplexer_1 (
    .in0(rd), .in1(2'b11), .in5(rt), .in6(rt), .in7(rt), .in10(rt), .in11(rt), .out(write), .sel(op));  // open: in2, in3, in4, in8, in9, in12, in13, in14, in15
  Multiplexer #(.select(4), .width(16), .enable("false")) multiplexer_2 (
    .in0(ALU_out), .in1(store), .in5(ALU_out), .in6(ALU_out), .in7(ALU_out), .in10(ALU_out), .in11(mem),
    .out(writeData), .sel(op));  // open: in2, in3, in4, in8, in9, in12, in13, in14, in15

  // Other names for the same wires on the sheet: alu[15:0] = ALU_out
endmodule

module Mem_Address (
  input  [15:0] rs,
  input  [7:0] imm,
  output [15:0] mem_addr
);

  wire [15:0] imm_extension_1_signed;

  imm_extension imm_extension_1 (.imm(imm), .\signed (imm_extension_1_signed));  // open: unsigned
  Adder #(.width(16)) adder_1 (.a(rs), .b(imm_extension_1_signed), .out(mem_addr));  // open: cin, cout

  // Notes on the sheet:
  //   imm extension
endmodule

module RegWrite (
  input  [3:0] opcode,
  output RegWrite
);

  Multiplexer #(.select(4), .enable("false")) multiplexer_1 (
    .in0(1'b1), .in1(1'b1), .in5(1'b1), .in6(1'b1), .in7(1'b1), .in10(1'b1), .in11(1'b1), .out(RegWrite),
    .sel(opcode));  // open: in2, in3, in4, in8, in9, in12, in13, in14, in15
endmodule

module Branch_Calc (
  input  beq,
  input  bne,
  input  [7:0] imm,
  input  [15:0] currPC,
  input  equal,
  output [15:0] branchPC,
  output branch
);

  wire and_1_out, and_2_out, not_1_out;
  wire [15:0] adder_1_out, imm_extension_1_signed;

  Adder #(.width(16)) adder_1 (.a(currPC), .b(16'h1), .out(adder_1_out));  // open: cin, cout
  imm_extension imm_extension_1 (.imm(imm), .\signed (imm_extension_1_signed));  // open: unsigned
  not not_1 (not_1_out, equal);
  Adder #(.width(16)) adder_2 (.a(imm_extension_1_signed), .b(adder_1_out), .out(branchPC));  // open: cin, cout
  and and_1 (and_1_out, beq, equal);
  and and_2 (and_2_out, bne, not_1_out);
  or or_1 (branch, and_1_out, and_2_out);

  // Other names for the same wires on the sheet: eq = equal

  // Notes on the sheet:
  //   imm extension
endmodule

module jumps (
  input  jal,
  input  j,
  input  jr,
  input  [11:0] target_addr,
  input  [15:0] currPC,
  input  [15:0] rs,
  output jump,
  output [15:0] jumpPC
);

  wire [15:0] and_1_out, next_calc;

  assign and_1_out = currPC & 16'hf000;  // AND_Gate and_1, 16 bits wide
  assign next_calc = {4'b0000, target_addr} | and_1_out;  // OR_Gate or_1, 16 bits wide
  Multiplexer #(.width(16), .enable("false")) multiplexer_1 (.in0(next_calc), .in1(rs), .out(jumpPC), .sel(jr));
  or or_2 (jump, jal, j, jr);
endmodule

module new_PC (
  input  [15:0] nextPC,
  input  [15:0] branchPC,
  input  branch,
  input  jump,
  input  [15:0] jumpPC,
  input  clk,
  output [15:0] newPC
);

  wire [15:0] adder_1_out, multiplexer_1_out, multiplexer_2_out;

  Adder #(.width(16)) adder_1 (.a(nextPC), .b(16'h1), .out(adder_1_out));  // open: cin, cout
  Multiplexer #(.width(16), .enable("false")) multiplexer_1 (
    .in0(adder_1_out), .in1(branchPC), .out(multiplexer_1_out), .sel(branch));
  Multiplexer #(.width(16), .enable("false")) multiplexer_2 (
    .in0(multiplexer_1_out), .in1(jumpPC), .out(multiplexer_2_out), .sel(jump));
  Register #(.width(16)) register_1 (.D(multiplexer_2_out), .Q(newPC), .clk(clk));  // open: en, clr
endmodule
